# Fritzing sketch Arduino LDR voltage divider (saved by Fritzing 0.6.5b)
breadboards: 1

parts:
  Arduino1 = Arduino
  R1 = Photocell (LDR) [package=THT]
  R2 = Resistor [tolerance=±5% resistance=470k package=THT]

nets:
  N1: Arduino1.GND, R2.Pin_1
  N2: Arduino1.+5V, R1.pin_0
  N3: Arduino1.A0, R1.pin_1, R2.Pin_0
