# Fritzing sketch protective diode (saved by Fritzing 0.7.0b)
breadboards: 1

parts:
  Arduino1 = Arduino
  VCC1 = Battery block 9V
  M1 = DC Motor
  Q1 = Basic FET N-Channel [package="TO220 [THT]"]
  D1 = Rectifier Diode [part_number=1N4001 package="300 mil [THT]"]

nets:
  N1: Arduino1.GND, VCC1.-, Q1.source
  N2: Arduino1.D5, Q1.gate
  N3: Arduino1.VIN, VCC1.+, M1.pin_1, D1.cathode
  N4: M1.pin_2, Q1.drain, D1.anode
